// Logisim project ALU_GroupXX.circ as structural Verilog: 5 circuits, main circuit main
module main (
  output halt,
  output [8:0] counter,
  output [3:0] op,
  output [11:0] a,
  output [11:0] b,
  output [11:0] oracle,
  output [11:0] result,
  output err_oracle,
  output error,
  output ok,
  output start_delimiter
);

  wire and_1_out, and_2_out, clock_1_out, comparator_1_eq, comparator_2_eq;

  Clock clock_1 (.out(clock_1_out));
  Counter #(.width(9), .max('h1ff), .trigger("falling")) counter_1 (
    .Q(counter), .carry(halt), .clk(clock_1_out));  // open: load, D, count, clr
  RAM #(.addrWidth(12), .dataWidth(4), .bus("separate")) ram_1 (
    .addr({counter, 3'b000}), .data(op), .ld(1'b1));  // open: din, str, sel, clk, clr
  RAM #(.addrWidth(12), .dataWidth(12), .bus("separate")) ram_2 (
    .addr({counter, 3'b001}), .data(a), .ld(1'b1));  // open: din, str, sel, clk, clr
  RAM #(.addrWidth(12), .dataWidth(12), .bus("separate")) ram_3 (
    .addr({counter, 3'b010}), .data(b), .ld(1'b1));  // open: din, str, sel, clk, clr
  RAM #(.addrWidth(12), .dataWidth(12), .bus("separate")) ram_4 (
    .addr({counter, 3'b011}), .data(oracle), .ld(1'b1));  // open: din, str, sel, clk, clr
  RAM #(.addrWidth(12), .dataWidth(1), .bus("separate")) ram_5 (
    .addr({counter, 3'b100}), .data(err_oracle), .ld(1'b1));  // open: din, str, sel, clk, clr
  RAM #(.addrWidth(12), .dataWidth(1), .bus("separate")) ram_6 (
    .addr({counter, 3'b101}), .data(start_delimiter), .ld(1'b1));  // open: din, str, sel, clk, clr
  _12_bit_ALU u_12_bit_alu_1 (.ALU_code(op), .a(a), .b(b), .overflow(error), .result(result));
  Comparator #(.width(1), .mode("unsigned")) comparator_1 (
    .a(error), .b(err_oracle), .eq(comparator_1_eq));  // open: gt, lt
  Comparator #(.width(12)) comparator_2 (.a(result), .b(oracle), .eq(comparator_2_eq));  // open: gt, lt
  and and_1 (and_1_out, comparator_1_eq, error);
  and and_2 (and_2_out, comparator_2_eq, comparator_1_eq, ~error);  // AND_Gate
  or or_1 (ok, and_1_out, and_2_out);

  // Notes on the sheet:
  //   You must complete the circuit '12-bit ALU' instead.
  //   DO NOT EDIT THIS CIRCUIT!
endmodule

module _12_bit_ALU (
  input  [3:0] ALU_code,
  input  [11:0] a,
  input  [11:0] b,
  output [11:0] result,
  output overflow
);

  wire n12_bit_adder_1_overflow, n12_bit_adder_2_overflow;
  wire [11:0] and_1_out, n12_bit_adder_1_sum, n12_bit_adder_2_sum, not_1_out, or_1_out;

  assign not_1_out = ~b;  // NOT_Gate not_1, 12 bits wide
  assign or_1_out = a | b;  // OR_Gate or_1, 12 bits wide
  assign and_1_out = b & a;  // AND_Gate and_1, 12 bits wide
  _12_Bit_Adder u_12_bit_adder_1 (.a(b), .b(a), .Sum(n12_bit_adder_1_sum), .Overflow(n12_bit_adder_1_overflow));
  _12_Bit_Adder u_12_bit_adder_2 (.a(a), .b(not_1_out), .Sum(n12_bit_adder_2_sum), .Overflow(n12_bit_adder_2_overflow));
  Multiplexer #(.select(4), .width(12), .enable("false")) multiplexer_1 (
    .in0({12{1'b0}}), .in1(or_1_out), .in2(and_1_out), .in3(n12_bit_adder_1_sum), .in4(n12_bit_adder_2_sum),
    .out(result), .sel(ALU_code));  // open: in5, in6, in7, in8, in9, in10, in11, in12, in13, in14, in15
  or or_2 (overflow, n12_bit_adder_1_overflow, n12_bit_adder_2_overflow);

  // Notes on the sheet:
  //   This circuit is used as a block in the main circuit, and its layout must remain unchanged. The circuit called "main" should be the main circuit of this file.
  //   Do not change the circuit appearance.
  //   DO NOT CHANGE THE INPUTS AND OUTPUTS OF THIS CIRCUIT!
  //   Do not add/remove inputs or outputs. Do not even change their location or orientation.
endmodule

module Less_than (
  input  [11:0] a,
  input  [11:0] b
);

  wire n12_bit_adder_1_overflow;
  wire [11:0] not_1_out;

  _12_Bit_Adder u_12_bit_adder_1 (.a(a), .b(not_1_out), .Overflow(n12_bit_adder_1_overflow));  // open: Sum
  assign not_1_out = ~b;  // NOT_Gate not_1, 12 bits wide
  Multiplexer #(.enable("false")) multiplexer_1 (.in1(1'b0), .sel(n12_bit_adder_1_overflow));  // open: in0, out
endmodule

module Equals (
  input  [11:0] a,
  input  [11:0] b
);

  wire [11:0] n12_bit_adder_1_sum, not_1_out;

  _12_Bit_Adder u_12_bit_adder_1 (.a(a), .b(not_1_out), .Sum(n12_bit_adder_1_sum));  // open: Overflow
  assign not_1_out = ~b;  // NOT_Gate not_1, 12 bits wide
  // OR_Gate or_1 is placed but not wired
endmodule

module Subtraction (
  input  [11:0] a,
  input  [11:0] b,
  output [11:0] out_3,
  output [11:0] out_4,
  output [11:0] out_5,
  output [11:0] out_6
);

  wire n12_bit_adder_2_overflow;

  assign out_3 = ~b;  // NOT_Gate not_1, 12 bits wide
  _12_Bit_Adder u_12_bit_adder_1 (.a(out_3), .b(12'h1), .Sum(out_5));  // open: Overflow
  _12_Bit_Adder u_12_bit_adder_2 (.a(a), .b(out_5), .Sum(out_4), .Overflow(n12_bit_adder_2_overflow));

  assign out_6 = 12'h1;
endmodule
